# Fritzing sketch fritzing_sketch (saved by Fritzing 0.9.0b)
breadboards: 1

parts:
  Raspberry_Pi_B_rev1 = Raspberry Pi B rev2
  Dynamixel_AX-12 = Basic Servo
  9_6V = Power plug
  IC1 = IC, DIP package, 20 pins [chip_label=74LS241]
  R1 = Resistor [tolerance=±5% resistance=10k package=THT]

nets:
  N1: Raspberry_Pi_B_rev1.5V, IC1.pin20, R1.Pin_1
  GND: Raspberry_Pi_B_rev1.GND, Dynamixel_AX-12.gnd, 9_6V.GND, IC1.pin10
  N2: Raspberry_Pi_B_rev1.GPIO_14, IC1.pin17
  N3: Raspberry_Pi_B_rev1.GPIO_15, IC1.pin18
  N4: Raspberry_Pi_B_rev1.GPIO_18, IC1.pin1, IC1.pin19
  VCC: Dynamixel_AX-12.vcc, 9_6V.VCC
  N5: Dynamixel_AX-12.pulse, IC1.pin2, IC1.pin3, R1.Pin_0
